// Logisim project CPUtest.circ as structural Verilog: 9 circuits, main circuit main
module main (
  input  [4:0] in_1,
  input  [9:0] in_2,
  input  [2:0] in_3,
  output [9:0] out_4,
  output [9:0] out_5,
  output [9:0] out_6,
  output [9:0] out_7,
  output [9:0] out_8,
  output [9:0] out_9,
  output [9:0] out_10,
  output ignore,
  output halt
);

  wire and_1_out, and_3_out, CLK, clock_1_out, comparator_1_lt, comparator_2_lt, Dec__Select, decoder_1_out8,
       decoder_1_out9, decoder_1_out10, decoder_1_out11, decoder_1_out12, not_1_out, not_2_out, NZ,
       PC_Select, t_ff_2_q, TClock;
  wire [1:0] counter_2_q, Upper_2_bits;
  wire [2:0] _3_bit_Opcode, A_Select, B, Decoder, or_1_out, rom_1_data;
  wire [3:3] B_Select;
  wire [4:0] counter_1_q, multiplexer_1_out, n5_bit_alu_1_add, PC_pc_output;
  wire [4:3] Control_Unit;
  wire [6:0] adder_1_out, adder_2_out, ASCII, LSB, MiddleBits;
  wire [7:0] multiplexer_4_out;
  wire [9:0] _10_bit_from_ALU, A, Data, multiplexer_3_out;

  _5_bit_Counter PC (.Data(n5_bit_alu_1_add), .PC_Output(PC_pc_output));
  assign or_1_out = in_3 | B;  // OR_Gate or_1, 3 bits wide
  _5_bit_ALU u_5_bit_alu_1 (.A(PC_pc_output), .B(multiplexer_1_out), .Add(n5_bit_alu_1_add));  // open: Cin, C5
  or or_2 (NZ, or_1_out[0], or_1_out[1], or_1_out[2]);
  Multiplexer #(.width(5)) multiplexer_1 (
    .in0(in_1), .in1(Data[4:0]), .out(multiplexer_1_out), .sel(PC_Select));  // open: en
  and and_1 (and_1_out, CLK, not_1_out);
  not not_1 (not_1_out, Control_Unit[4]);
  Decoder #(.select(4)) decoder_1 (
    .out8(decoder_1_out8), .out9(decoder_1_out9), .out10(decoder_1_out10), .out11(decoder_1_out11),
    .out12(decoder_1_out12), .sel({Control_Unit[3], _3_bit_Opcode}));  // open: out0, out1, out2, out3, out4, out5, out6, out7, out13, out14, out15, en
  RAM #(.addrWidth(5), .dataWidth(24)) ram_1 (
    .addr(PC_pc_output), .data({Control_Unit, _3_bit_Opcode, Decoder, A_Select, B, Data}), .clk(and_1_out));  // open: sel, ld, clr
  or or_3 (B_Select[3], decoder_1_out8, decoder_1_out9, decoder_1_out10);
  Register_Bank register_bank_1 (
    .Opcode(Dec__Select), .Decoder_Input(Decoder), ._10_bit_from_ALU(_10_bit_from_ALU), .R0(out_4),
    .R1(out_5), .R2(out_6), .R3(out_7), .R4(out_8), .R5(out_9), .R6(out_10));
  Multiplexer #(.select(3), .width(10)) multiplexer_2 (
    .in0(out_4), .in1(out_5), .in2(out_6), .in3(out_7), .in4(out_8), .in5(out_9), .in6(out_10), .out(A),
    .sel(A_Select));  // open: in7, en
  _10_bit_ALU u_10_bit_alu_1 (
    .MUX_Switch(B_Select[3]), .Opcode(_3_bit_Opcode), .A(A), .B(multiplexer_3_out),
    ._10_bits_from_ALU(_10_bit_from_ALU));  // open: Cin, Cin_2
  Multiplexer #(.select(4), .width(10)) multiplexer_3 (
    .in0(out_4), .in1(out_5), .in2(out_6), .in3(out_7), .in4(out_8), .in5(out_9), .in6(out_10), .in7(in_2),
    .in8(Data), .in9(Data), .in10(Data), .in11(Data), .in12(Data), .in13(Data), .in14(Data), .in15(Data),
    .out(multiplexer_3_out), .sel({B_Select[3], B}));  // open: en
  and and_2 (PC_Select, NZ, decoder_1_out11);
  nor nor_1 (Dec__Select, decoder_1_out12, decoder_1_out11);
  TTY #(.rows(33), .cols(4)) tty_1 (.data(ASCII), .clk(TClock));  // open: we, clr
  // Probe on out_4
  // Probe on out_8
  Counter #(.width(5), .max('h1f), .ongoal("stay")) counter_1 (
    .Q(counter_1_q), .carry(halt), .clk(CLK));  // open: load, D, count, clr
  // Probe on out_5
  // Probe on out_9
  Multiplexer #(.select(3), .width(10)) multiplexer_4 (
    .in0(out_4), .in1(out_5), .in2(out_6), .in3(out_7), .in4(out_8), .in5(out_9), .in6(out_10),
    .out({Upper_2_bits, multiplexer_4_out}), .sel(rom_1_data));  // open: in7, en
  not not_2 (not_2_out, halt);
  Clock clock_1 (.out(clock_1_out));
  ROM #(.addrWidth(5), .dataWidth(3)) rom_1 (.addr(counter_1_q), .data(rom_1_data));  // open: sel
  and and_3 (and_3_out, not_2_out, clock_1_out);
  not not_3 (TClock, and_3_out);
  // Probe on out_6
  // Probe on out_10
  // Probe on out_7
  Comparator #(.width(7)) comparator_1 (
    .a(7'b0111001), .b({3'b011, multiplexer_4_out[3:0]}), .lt(comparator_1_lt));  // open: gt, eq
  Comparator #(.width(7)) comparator_2 (
    .a(7'b0111001), .b({3'b011, multiplexer_4_out[7:4]}), .lt(comparator_2_lt));  // open: gt, eq
  T_Flip_Flop t_ff_1 (.clk(t_ff_2_q), .T(1'b1), .Q(CLK));  // open: Qn, preset, reset, en
  T_Flip_Flop t_ff_2 (.clk(and_3_out), .T(1'b1), .Q(t_ff_2_q));  // open: Qn, preset, reset, en
  Adder_part #(.width(7)) adder_1 (
    .a({3'b011, multiplexer_4_out[3:0]}), .b(7'b0000111), .out(adder_1_out));  // open: cin, cout
  Adder_part #(.width(7)) adder_2 (
    .a({3'b011, multiplexer_4_out[7:4]}), .b(7'b0000111), .out(adder_2_out));  // open: cin, cout
  Multiplexer #(.select(2), .width(7)) multiplexer_5 (
    .in0({5'b01100, Upper_2_bits}), .in1(MiddleBits), .in2(LSB), .in3(7'b0100000), .out(ASCII),
    .sel(counter_2_q));  // open: en
  Counter #(.width(2), .max('h3)) counter_2 (.Q(counter_2_q), .clk(TClock));  // open: load, D, count, carry, clr
  Multiplexer #(.width(7), .disabled(0), .enable("false")) multiplexer_6 (
    .in0({3'b011, multiplexer_4_out[3:0]}), .in1(adder_1_out), .out(LSB), .sel(comparator_1_lt));
  Multiplexer #(.width(7), .disabled(0), .enable("false")) multiplexer_7 (
    .in0({3'b011, multiplexer_4_out[7:4]}), .in1(adder_2_out), .out(MiddleBits), .sel(comparator_2_lt));
  T_Flip_Flop t_ff_3 (.clk(CLK), .T(1'b1), .Q(ignore));  // open: Qn, preset, reset, en

  // Other names for the same wires on the sheet: Opcode[4:0] = {Control_Unit, _3_bit_Opcode};
  //   Control_Unit[2:0] = _3_bit_Opcode; B_Select[2:0] = B; Data_Switch = B_Select[3]; MUX_Switch = B_Select[3];
  //   HALT_t = Control_Unit[4]; R0[9:0] = out_4; R1[9:0] = out_5; R2[9:0] = out_6; R3[9:0] = out_7; R4[9:0] = out_8;
  //   R5[9:0] = out_9; R6[9:0] = out_10

  // Notes on the sheet:
  //   Register Bank
  //   DO NOT PUT ANY PINS ON THE main circuit.  (You should not need any anyway.)
  //   0F5
  //   0F5
  //   25A
  //   050
  //   2FF
  //   30A
  //   34F
  //   0F5
  //   1EA
  //   07A
  //   29B
  //   165
  //   10F
  //   0F5
  //   0AA
  //   0AA
  //   05A
  //   00A
  //   0FA
  //   104
  //   0B4
  //   165
  //   165
  //   001
  //   001
  //   000
  //   000
  //   000
  //   000
  //   000
  //   ???
  //   There is no Reset.  Just Ctrl-r, then load test.txt into your RAM, and then Ctrl-k
  //   You must  use the CLK tunnel for the source of your clock.  R0-R6 are the other tunnels you need to connect
  //   contents of rom_1 (hex, n*v repeats v):
  //   0 0 0 1 2 3 4 5 6 2 3 4 5 6 0 0 0 1 3 4 6 3 5 5 8*6
endmodule

module Adder (
  input  A,
  input  B,
  input  Cin,
  output S,
  output Cout
);

  wire and_1_out, and_2_out, xor_1_out;

  xor xor_1 (xor_1_out, A, B);
  and and_1 (and_1_out, A, B);
  xor xor_2 (S, xor_1_out, Cin);
  and and_2 (and_2_out, xor_1_out, Cin);
  or or_1 (Cout, and_2_out, and_1_out);
endmodule

module _5_bit_CLA (
  input  [4:0] A,
  input  [4:0] B,
  input  Cin,
  output [4:0] Sum,
  output C5
);

  wire C1, C2, C3, C4;

  Adder adder_1 (.A(A[0]), .B(B[0]), .Cin(Cin), .S(Sum[0]), .Cout(C1));
  Adder adder_2 (.A(A[1]), .B(B[1]), .Cin(C1), .S(Sum[1]), .Cout(C2));
  Adder adder_3 (.A(A[2]), .B(B[2]), .Cin(C2), .S(Sum[2]), .Cout(C3));
  Adder adder_4 (.A(A[3]), .B(B[3]), .Cin(C3), .S(Sum[3]), .Cout(C4));
  Adder adder_5 (.A(A[4]), .B(B[4]), .Cin(C4), .S(Sum[4]), .Cout(C5));

  // Other names for the same wires on the sheet: S0 = Sum[0]; S1 = Sum[1]; S2 = Sum[2]; S3 = Sum[3]; S4 = Sum[4]
endmodule

// ALU
module _5_bit_ALU (
  input  [4:0] A,
  input  [4:0] B,
  input  Cin,
  output [4:0] Add,
  output C5
);

  // _5_bit_CLA 5_bit_cla_1: pin names not known; wires that end beside it: Add, C5, Cin, A, B

  // Notes on the sheet:
  //   Input
endmodule

module Register_Bank (
  input  Opcode,
  input  [2:0] Decoder_Input,
  output [9:0] R0,
  output [9:0] R1,
  output [9:0] R2,
  output [9:0] R3,
  output [9:0] R4,
  output [9:0] R5,
  output [9:0] R6,
  output [9:0] _10_bit_from_ALU
);

  wire clock_1_out, decoder_1_out0, decoder_1_out1, decoder_1_out2, decoder_1_out3, decoder_1_out4,
       decoder_1_out5, decoder_1_out6;

  Decoder #(.select(3)) decoder_1 (
    .out0(decoder_1_out0), .out1(decoder_1_out1), .out2(decoder_1_out2), .out3(decoder_1_out3),
    .out4(decoder_1_out4), .out5(decoder_1_out5), .out6(decoder_1_out6), .sel(Decoder_Input), .en(Opcode));  // open: out7
  Clock clock_1 (.out(clock_1_out));
  _10_bit_Register u_10_bit_register_1 (
    .Output(R0), .Decoder(decoder_1_out0), ._10_bit_data(_10_bit_from_ALU), .Clock(clock_1_out));
  _10_bit_Register u_10_bit_register_2 (
    .Output(R1), .Decoder(decoder_1_out1), ._10_bit_data(_10_bit_from_ALU), .Clock(clock_1_out));
  _10_bit_Register u_10_bit_register_3 (
    .Output(R2), .Decoder(decoder_1_out2), ._10_bit_data(_10_bit_from_ALU), .Clock(clock_1_out));
  _10_bit_Register u_10_bit_register_4 (
    .Output(R3), .Decoder(decoder_1_out3), ._10_bit_data(_10_bit_from_ALU), .Clock(clock_1_out));
  _10_bit_Register u_10_bit_register_5 (
    .Output(R4), .Decoder(decoder_1_out4), ._10_bit_data(_10_bit_from_ALU), .Clock(clock_1_out));
  _10_bit_Register u_10_bit_register_6 (
    .Output(R5), .Decoder(decoder_1_out5), ._10_bit_data(_10_bit_from_ALU), .Clock(clock_1_out));
  _10_bit_Register u_10_bit_register_7 (
    .Output(R6), .Decoder(decoder_1_out6), ._10_bit_data(_10_bit_from_ALU), .Clock(clock_1_out));
endmodule

module _5_bit_Counter (
  input  [4:0] Data,
  output [4:0] PC_Output
);

  wire clock_1_out;

  Clock clock_1 (.out(clock_1_out));
  D_Flip_Flop d_ff_1 (.clk(clock_1_out), .D(Data[0]), .Q(PC_Output[0]), .en(1'b1));  // open: Qn, preset, reset
  D_Flip_Flop d_ff_2 (.clk(clock_1_out), .D(Data[1]), .Q(PC_Output[1]), .en(1'b1));  // open: Qn, preset, reset
  D_Flip_Flop d_ff_3 (.clk(clock_1_out), .D(Data[2]), .Q(PC_Output[2]), .en(1'b1));  // open: Qn, preset, reset
  D_Flip_Flop d_ff_4 (.clk(clock_1_out), .D(Data[3]), .Q(PC_Output[3]), .en(1'b1));  // open: Qn, preset, reset
  D_Flip_Flop d_ff_5 (.clk(clock_1_out), .D(Data[4]), .Q(PC_Output[4]), .en(1'b1));  // open: Qn, preset, reset

  // Notes on the sheet:
  //   5-bit Program Counter
endmodule

module _10_bit_Register (
  input  Clock,
  input  Decoder,
  input  [9:0] _10_bit_data,
  output [9:0] Output
);

  wire d_ff_6_qn;

  D_Flip_Flop d_ff_1 (.clk(Clock), .D(_10_bit_data[0]), .Q(Output[0]), .en(Decoder));  // open: Qn, preset, reset
  D_Flip_Flop d_ff_2 (.clk(Clock), .D(_10_bit_data[1]), .Q(Output[1]), .en(Decoder));  // open: Qn, preset, reset
  D_Flip_Flop d_ff_3 (.clk(Clock), .D(_10_bit_data[2]), .Q(Output[2]), .en(Decoder));  // open: Qn, preset, reset
  D_Flip_Flop d_ff_4 (.clk(Clock), .D(_10_bit_data[3]), .Q(Output[3]), .en(Decoder));  // open: Qn, preset, reset
  D_Flip_Flop d_ff_5 (.clk(Clock), .D(_10_bit_data[4]), .Q(Output[4]), .en(Decoder));  // open: Qn, preset, reset
  D_Flip_Flop d_ff_6 (
    .clk(Clock), .D(_10_bit_data[5]), .Q(Output[5]), .Qn(d_ff_6_qn), .en(Decoder));  // open: preset, reset
  D_Flip_Flop d_ff_7 (.clk(Clock), .D(_10_bit_data[6]), .Q(Output[6]), .en(Decoder));  // open: Qn, preset, reset
  D_Flip_Flop d_ff_8 (.clk(Clock), .D(_10_bit_data[7]), .Q(Output[7]), .en(Decoder));  // open: Qn, preset, reset
  D_Flip_Flop d_ff_9 (.clk(Clock), .D(_10_bit_data[8]), .Q(Output[8]), .en(Decoder));  // open: Qn, preset, reset
  D_Flip_Flop d_ff_10 (.clk(Clock), .D(_10_bit_data[9]), .Q(Output[9]), .en(Decoder));  // open: Qn, preset, reset
endmodule

// ALU
module _10_bit_ALU (
  input  [9:0] A,
  input  [9:0] B,
  input  [9:0] _10_bits_from_ALU,
  input  Cin,
  input  Cin_2,
  input  MUX_Switch,
  input  [2:0] Opcode
);

  wire n10_bit_cla_1_c10, n10_bit_cla_2_c10, not_3_out;
  wire [0:0] SRL;
  wire [9:0] ADD, AND, multiplexer_1_out, multiplexer_2_out, NOT, not_2_out, OR, SUB;
  wire [9:9] SLL;

  assign NOT = ~A;  // NOT_Gate not_1, 10 bits wide
  assign AND = A & B;  // AND_Gate and_1, 10 bits wide
  assign OR = A | B;  // OR_Gate or_1, 10 bits wide
  _10_bit_CLA u_10_bit_cla_1 (.Cin(Cin), .C10(n10_bit_cla_1_c10), .A(A), .B(B), .Sum(ADD));
  _10_bit_CLA u_10_bit_cla_2 (.Cin(Cin_2), .C10(n10_bit_cla_2_c10), .A(A), .B(not_2_out), .Sum(SUB));
  assign not_2_out = ~B;  // NOT_Gate not_2, 10 bits wide
  Multiplexer #(.select(3), .width(10)) multiplexer_1 (
    .in0(AND), .in1(OR), .in2(NOT), .in3(ADD), .in4(A), .in5({SLL[9], A[9:1]}), .in6({A[8:0], SRL[0]}),
    .in7(SUB), .out(multiplexer_1_out), .sel(Opcode), .en(not_3_out));
  not not_3 (not_3_out, MUX_Switch);
  Multiplexer #(.select(2), .width(10)) multiplexer_2 (
    .in0(AND), .in1(SUB), .in2(A), .out(multiplexer_2_out), .sel(Opcode[1:0]), .en(MUX_Switch));  // open: in3
  assign _10_bits_from_ALU = multiplexer_1_out ^ multiplexer_2_out;  // XOR_Gate xor_1, 10 bits wide

  // Other names for the same wires on the sheet: _2_Bit_Opcode[1:0] = Opcode[1:0]; _3_Bit_Opcode[2:0] = Opcode;
  //   MUX_Enable = MUX_Switch; MOV[9:0] = A; SLL[8:0] = A[9:1]; SRL[9:1] = A[8:0]
endmodule

module _10_bit_CLA (
  input  [9:0] A,
  input  Cin,
  input  [9:0] B,
  output [9:0] Sum,
  output C10
);

  wire adder_10_cout, C1, C2, C3, C4, C5, C6, C7, C8, C9;

  Adder adder_1 (.A(A[0]), .B(B[0]), .Cin(Cin), .S(Sum[0]), .Cout(C1));
  Adder adder_2 (.A(A[1]), .B(B[1]), .Cin(C1), .S(Sum[1]), .Cout(C2));
  Adder adder_3 (.A(A[2]), .B(B[2]), .Cin(C2), .S(Sum[2]), .Cout(C3));
  Adder adder_4 (.A(A[3]), .B(B[3]), .Cin(C3), .S(Sum[3]), .Cout(C4));
  Adder adder_5 (.A(A[4]), .B(B[4]), .Cin(C4), .S(Sum[4]), .Cout(C5));
  Adder adder_6 (.A(A[5]), .B(B[5]), .Cin(C5), .S(Sum[5]), .Cout(C6));
  Adder adder_7 (.A(A[6]), .B(B[6]), .Cin(C6), .S(Sum[6]), .Cout(C7));
  Adder adder_8 (.A(A[7]), .B(B[7]), .Cin(C7), .S(Sum[7]), .Cout(C8));
  Adder adder_9 (.A(A[8]), .B(B[8]), .Cin(C8), .S(Sum[8]), .Cout(C9));
  Adder adder_10 (.A(A[9]), .B(B[9]), .Cin(C9), .S(Sum[9]), .Cout(adder_10_cout));

  // Other names for the same wires on the sheet: S0 = Sum[0]; S1 = Sum[1]; S2 = Sum[2]; S3 = Sum[3]; S4 = Sum[4];
  //   S5 = Sum[5]; S6 = Sum[6]; S7 = Sum[7]; S8 = Sum[8]; S9 = Sum[9]
endmodule
