// Logisim project alu.circ as structural Verilog: 3 circuits, main circuit main
module main (
);

  wire C0, C1, C2, C3, C4, C5, CIN, clock_1_out, clock_2_out, go, HCLK, not_2_out, reset, S0, S1;
  wire [2:0] multiplexer_2_out;
  wire [4:0] A, ADD, AND, B, NOT, OR;
  wire [6:1] counter_1_q;

  assign NOT = ~A;  // NOT_Gate not_1, 5 bits wide
  assign AND = A & B;  // AND_Gate and_1, 5 bits wide
  assign OR = A | B;  // OR_Gate or_1, 5 bits wide
  CLA cla_1 (.Cin(CIN), .A(A), .B(B), .S0(ADD[0]), .S1(ADD[1]), .S2(ADD[2]), .S3(ADD[3]), .S4(ADD[4]), .C5(C5));
  Multiplexer #(.select(2), .width(5)) multiplexer_1 (
    .in0(AND), .in1(OR), .in2(NOT), .in3(ADD), .out({C4, C3, C2, C1, C0}), .sel({S1, S0}));  // open: en
  // Probe on {C5, C4, C3}
  // Probe on {C2, C1, C0}
  Multiplexer #(.width(3)) multiplexer_2 (
    .in0({C5, C4, C3}), .in1({C2, C1, C0}), .out(multiplexer_2_out), .sel(HCLK));  // open: en
  // Probe on multiplexer_2_out
  // Probe on {4'b0110, multiplexer_2_out}
  TTY #(.rows(32), .cols(2)) tty_1 (.data({4'b0110, multiplexer_2_out}), .clk(clock_1_out), .we(go), .clr(reset));
  Clock clock_1 (.out(clock_1_out));
  // Probe on {A, CIN}
  // Probe on B
  // Probe on S1
  Counter #(.width(7), .max('h7f), .ongoal("stay")) counter_1 (
    .Q({counter_1_q, HCLK}), .clk(clock_2_out), .clr(reset));  // open: load, D, count, carry
  Clock clock_2 (.out(clock_2_out));
  // Probe on S0
  not not_2 (not_2_out, HCLK);
  Button u_Reset (.out(reset));
  Random #(.width(13), .seed(34573)) random_1 (.clk(not_2_out), .next(go), .out({B, A, CIN, S1, S0}), .clr(reset));
  not not_3 (go, counter_1_q[6]);

  // Notes on the sheet:
  //   07
  //   51
  //   40
  //   51
  //   77
  //   77
  //   57
  //   63
  //   43
  //   77
  //   60
  //   51
  //   46
  //   71
  //   32
  //   43
  //   34
  //   50
  //   53
  //   00
  //   07
  //   02
  //   74
  //   04
  //   35
  //   52
  //   52
  //   50
  //   65
  //   46
  //   11
  //   57
endmodule

module FULL_ADDER (
  input  A,
  input  B,
  input  Cin,
  output S,
  output Cout
);

  wire and_1_out, and_2_out, xor_1_out;

  xor xor_1 (xor_1_out, A, B);
  and and_1 (and_1_out, A, B);
  xor xor_2 (S, xor_1_out, Cin);
  and and_2 (and_2_out, xor_1_out, Cin);
  or or_1 (Cout, and_2_out, and_1_out);
endmodule

module CLA (
  input  [4:0] A,
  input  [4:0] B,
  input  Cin,
  output S0,
  output S1,
  output S2,
  output S3,
  output S4,
  output C5
);

  wire C1, C2, C3, C4;

  FULL_ADDER full_adder_1 (.A(A[0]), .B(B[0]), .Cin(Cin), .S(S0), .Cout(C1));
  FULL_ADDER full_adder_2 (.A(A[1]), .B(B[1]), .Cin(C1), .S(S1), .Cout(C2));
  FULL_ADDER full_adder_3 (.A(A[2]), .B(B[2]), .Cin(C2), .S(S2), .Cout(C3));
  FULL_ADDER full_adder_4 (.A(A[3]), .B(B[3]), .Cin(C3), .S(S3), .Cout(C4));
  FULL_ADDER full_adder_5 (.A(A[4]), .B(B[4]), .Cin(C4), .S(S4), .Cout(C5));
endmodule
